# Fritzing sketch gözlük şema (saved by Fritzing 0.9.3b)
circuit board: 24.2989cm x 19.3847cm

parts:
  Micro_USB = TP4056 [chip_label=TP4056 package="DIP (Dual Inline) [THT]"]
  STEP_UP_5V = mini boost module
  Q1 = NPN-Transistor [package="TO92 [THT]"]
  R1 = Resistor [tolerance=±5% resistance=220 package="2010 [SMD]"]
  S1 = SPST Slide Switch [package="SIP THT"]
  LED2 = LEDs [package=led10mm]
  TP2 = TEST-POINT [package=pad.02x.02]
  TP1 = TEST-POINT [package=pad.02x.02]
  IC1 = Voltage Regulator AMS1117 [package=sot223]
  C1 = Capacitor Polarized [part_number="25V 10μF" package=cpol-radial-10uf-25v]
  C2 = Ceramic Capacitor [capacitance=0.1µF part_number=6.3V package="1206 [SMD, multilayer]"]
  C3 = Capacitor Polarized [part_number="25V 10μF" package=cpol-radial-10uf-25v]
  Mod1 = ESP32 - CAM
  MCU3 = ESP-WROOM-32 [ESP-32S] Module [part_number=ESP-WROOM-32]
  U2 = IC, SIP package, 6 pins [chip_label="BT Headset PCB"]
  Q2 = NPN-Transistor [package="TO92 [THT]"]
  LeftSPK = Header 2 [package=jst-2-smd]
  RightSPK = Header 2 [package=jst-2-smd]
  LED1 = LEDs [package=led10mm]
  R3 = Resistor [tolerance=±5% resistance=220 package="0402 [SMD]"]
  BAT1 = 18650 battery holder [part_number="3.7V 18650" package=battery-18650-kit]
  D1 = Rectifier Diode [part_number=1N4001 package="300 mil [THT]"]
  C4 = Ceramic Capacitor [capacitance=0.1µF part_number=6.3V package="1206 [SMD, multilayer]"]
  U1 = Vibration Motor- ROB-08449 [package=vibe-motor-10mm]
  R2 = Resistor [tolerance=±5% resistance=10k package="0402 [SMD]"]

nets:
  N1: Micro_USB.pin3, S1.COM
  N2: Micro_USB.pin4, BAT1.-
  N3: Micro_USB.pin5, BAT1.+
  N4: Micro_USB.pin6, STEP_UP_5V.Pin_1
  N5: STEP_UP_5V.Pin_2, S1.L2
  GND: STEP_UP_5V.Pin_3, LED2.C, IC1.GND, C1.-, C2.1, C3.-, Mod1.GND, LED1.C, C4.1
  N6: STEP_UP_5V.Pin_4, IC1.IN, C1.+, C2.0, Mod1.5V
  N7: Q1.E, MCU3.Pin_1, MCU3.Pin_15, U2.pin1, Q2.E
  N8: Q1.B, R1.Pin_0
  N9: Q1.C, D1.anode, U1.-
  N10: R1.Pin_1, MCU3.Pin_23
  N11: LED2.A, MCU3.Pin_10
  N12: TP2.1, MCU3.Pin_9
  N13: TP1.1, MCU3.Pin_8
  N14: IC1.OUT, C3.+, C4.0
  N15: Mod1.VOT, MCU3.Pin_34
  N16: Mod1.VOR, MCU3.Pin_35
  N17: MCU3.Pin_2, D1.cathode, U1.+, R2.Pin_1
  N18: MCU3.Pin_3, R2.Pin_0
  N19: MCU3.Pin_14, LED1.A
  N20: MCU3.Pin_24, R3.Pin_0
  N21: U2.pin2, Q2.C
  N22: U2.pin3, LeftSPK.1
  N23: U2.pin4, LeftSPK.2
  N24: U2.pin5, RightSPK.1
  N25: U2.pin6, RightSPK.2
  N26: Q2.B, R3.Pin_1

custom parts:
  TP4056: A DIP stand-in part for whatever IC you want. With 6 pins on a 300mil dual inline package (DIP) footprint.
  mini boost module: mini boost module.
  SPST Slide Switch: SPST slide switch with inline 100mil spacing through hole connection terminals
  ESP32 - CAM: The ESP32-CAM has a very competitive small-size camera module that can operate independently as a minimum system with a footprint of only 27*40.5*4.5mm and a deep sleep current of up to 6mA.
  ESP-WROOM-32 [ESP-32S] Module: Espressif ESP-WROOM-32 WiFi/Bluetooth LE microcontroller module also known as the Ai-Thinker ESP-32S module with similar formfactor. The ESP32 is a microcontroller chip with WiFi and BLE capabilities. The chip is developed by Espressif and is the successor to the popular ESP8266 WiFi module.
  18650 battery holder: 18650 Battery
